# Fritzing sketch temperature_humidity_lcd_arduino_shield (saved by Fritzing 0.9.9b)
circuit board: 8.5cm x 7cm
breadboards: 1

parts:
  LCD = Standard LCD 16x2 white on blue [part_number=181]
  P = Trimmer Potentiometer [maximum_resistance=10kΩ package=THT]
  R = Resistor [tolerance=±5% power=0.25 resistance=220 package=THT]
  SHT40 = Adafruit SHT40
  Part1 = Arduino Uno (Rev3)

nets:
  GND: LCD.VSS, LCD.R/W, LCD.LED-, P.leg2, SHT40.GND, Part1.GND
  VDD: LCD.VDD, P.leg1, R.Pin_0, SHT40.VCC, Part1.5V
  N1: LCD.V0, P.wiper
  N2: LCD.RS, Part1.D2
  N3: LCD.E, Part1.D3_PWM
  N4: LCD.DB4, Part1.D10_PWM/SS
  N5: LCD.DB5, Part1.D11_PWM/MOSI
  N6: LCD.DB6, Part1.D12/MISO
  N7: LCD.DB7, Part1.D13/SCK
  N8: LCD.LED+, R.Pin_1
  N9: SHT40.SCL, Part1.A5/SCL
  N10: SHT40.SDA, Part1.A4/SDA

custom parts:
  Standard LCD 16x2 white on blue: Standard HD44780 LCDs are useful for creating standalone projects. * 16 characters wide, 2 rows * White text on blue background * Connection port is 0.1" pitch, single row for easy breadboarding and wiring
  Adafruit SHT40: Sensirion Temperature/Humidity sensors are some of the finest & highest-accuracy devices you can get. And finally, we have some that have a true I2C interface for easy reading. The SHT40 sensor is the fourth generation (started at the SHT10 and worked its way up to the top!). The SHT40 has an excellent ±1.8% typical relative humidity accuracy from 25 to 75% and ±0.2 °C typical accuracy from 0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
